# Fritzing sketch KY-001 Temperature Sensor (saved by Fritzing 0.9.3b)

parts:
  Pico1 = Raspberry Pi Pico
  Part1 = KY-001 Temperature Sensor Module [package="Breakout board"]

nets:
  3V3: Pico1.3V3, Part1.Vin
  N1: Pico1.GP28_A2, Part1.S
  N2: Pico1.GND, Part1.-

custom parts:
  Raspberry Pi Pico: Raspberry Pi Pico. Based around the RP2040 microcontroller the Pico is a low cost microcontroller device bringing Raspberry Pi quality, cost, and easy of use to the microcontroller space.
  KY-001 Temperature Sensor Module: Arduino Temperature Sensor Module Keyes KY-001, Allows ambient temperature measurement using digital serial bus (DS18B20)
