# Fritzing sketch KY-003 Hall Magnetic Sensor (saved by Fritzing 0.9.3b)

parts:
  Pico1 = Raspberry Pi Pico
  Part1 = KY-003 Hall Magnetic Sensor Module [package="Breakout board"]

nets:
  N1: Pico1.GND, Part1.-
  3V3: Pico1.3V3, Part1.Vin
  N2: Pico1.GP28_A2, Part1.S

custom parts:
  Raspberry Pi Pico: Raspberry Pi Pico. Based around the RP2040 microcontroller the Pico is a low cost microcontroller device bringing Raspberry Pi quality, cost, and easy of use to the microcontroller space.
  KY-003 Hall Magnetic Sensor Module: KEYES KY-003 Arduino Hall Magnetic Sensor Module is a switch that will turn on/off in the presence of a magnetic field.
