# Fritzing sketch KY-006 Passive Buzzer (saved by Fritzing 0.9.3b)

parts:
  Pico1 = Raspberry Pi Pico
  Mod4 = KY-012 Active Buzzer Module [package="Breakout board"]

nets:
  N1: Pico1.3V3, Mod4.NC
  N2: Pico1.GP28_A2, Mod4.S
  N3: Pico1.GND, Mod4.-

custom parts:
  Raspberry Pi Pico: Raspberry Pi Pico. Based around the RP2040 microcontroller the Pico is a low cost microcontroller device bringing Raspberry Pi quality, cost, and easy of use to the microcontroller space.
  KY-012 Active Buzzer Module: Active Piezoelectric Buzzer Module KY-012, it produces single-tone sound when signal is high. (Special thanks to vanepp for fixing the PCB holes and other errors)
