# Fritzing sketch KY-009_SMD_RGB (saved by Fritzing 0.9.3b)

parts:
  Pico1 = Raspberry Pi Pico
  Part1 = KY-009 Full Color RGB LED SMD Module [package="Breakout board"]

nets:
  N1: Pico1.GND, Part1.-
  N2: Pico1.GP2, Part1.B
  N3: Pico1.GP1, Part1.G
  N4: Pico1.GP0, Part1.R

custom parts:
  Raspberry Pi Pico: Raspberry Pi Pico. Based around the RP2040 microcontroller the Pico is a low cost microcontroller device bringing Raspberry Pi quality, cost, and easy of use to the microcontroller space.
  KY-009 Full Color RGB LED SMD Module: RGB full color LED Module KY-009 for Arduino, emits a range of colors by mixing red, green and blue. The amount of each primary color is adjusted using PWM.
