# Fritzing sketch KY-021 Mini Magnetic Reed Switch (saved by Fritzing 0.9.3b)

parts:
  Pico1 = Raspberry Pi Pico
  Part2 = KY-021 Mini Magnetic Reed Switch Module [package="Breakout board"]

nets:
  N1: Pico1.GND, Part2.-
  3V3: Pico1.3V3, Part2.Vin
  N2: Pico1.GP28_A2, Part2.S

custom parts:
  Raspberry Pi Pico: Raspberry Pi Pico. Based around the RP2040 microcontroller the Pico is a low cost microcontroller device bringing Raspberry Pi quality, cost, and easy of use to the microcontroller space.
  KY-021 Mini Magnetic Reed Switch Module: KY-021 magnetic reed switch module. A reed switch is a magnetic sensor that is normally open and gets closed when exposed to a magnetic field.
