# Fritzing sketch KY-029_2_Color (saved by Fritzing 0.9.3b)

parts:
  Pico1 = Raspberry Pi Pico
  Part1 = KY-011 Two Color LED Module [package="Breakout board"]
  R1 = Resistor [tolerance=±5% resistance=150 package=THT]
  R2 = Resistor [tolerance=±5% resistance=150 package=THT]

nets:
  N1: Pico1.GND, Part1.-
  N2: Pico1.GP1, R1.Pin_1
  N3: Pico1.GP0, R2.Pin_1
  N4: Part1.S, R1.Pin_0
  N5: Part1.Vin, R2.Pin_0

custom parts:
  Raspberry Pi Pico: Raspberry Pi Pico. Based around the RP2040 microcontroller the Pico is a low cost microcontroller device bringing Raspberry Pi quality, cost, and easy of use to the microcontroller space.
  KY-011 Two Color LED Module: KEYES KY-011 Two Color LED Module consist of a common cathode 3mm red/green LED.
