# Fritzing sketch KY-031_Knock_Sensor (saved by Fritzing 0.9.3b)

parts:
  Pico1 = Raspberry Pi Pico
  Mod1 = KY-031 Knock Sensor Module [package="Breakout board"]

nets:
  3V3: Pico1.3V3, Mod1.Vin
  N1: Pico1.GP28_A2, Mod1.S
  N2: Pico1.GND, Mod1.-

custom parts:
  Raspberry Pi Pico: Raspberry Pi Pico. Based around the RP2040 microcontroller the Pico is a low cost microcontroller device bringing Raspberry Pi quality, cost, and easy of use to the microcontroller space.
  KY-031 Knock Sensor Module: KY-031 Knock Sensor module. A vibration sensor that sends a signal when a knock/tap is detected.
