# Fritzing sketch KY-032 OBSTACLE DETECTOR (saved by Fritzing 0.9.3b)

parts:
  Pico1 = Raspberry Pi Pico
  Mod3 = KY-032 IR Obstacle Avoidance Sensor Module [package="Breakout board"]

nets:
  N1: Pico1.3V3, Mod3.+
  N2: Pico1.GP27_A1, Mod3.out
  GND: Pico1.GND, Mod3.GND

custom parts:
  Raspberry Pi Pico: Raspberry Pi Pico. Based around the RP2040 microcontroller the Pico is a low cost microcontroller device bringing Raspberry Pi quality, cost, and easy of use to the microcontroller space.
  KY-032 IR Obstacle Avoidance Sensor Module: KY-032 Infrared Obstacle Avoidance Sensor. Distance-adjustable, infrared proximity sensor designed for wheeled robots. Also known as AD-032.
