# Fritzing sketch KY-033 Line Detector (saved by Fritzing 0.9.3b)

parts:
  Pico1 = Raspberry Pi Pico
  Mod2 = KY-033 Line Tracking Sensor Module [package="Breakout board"]

nets:
  3V3: Pico1.3V3, Mod2.VCC
  N1: Pico1.GP27_A1, Mod2.OUT
  GND: Pico1.GND, Mod2.GND

custom parts:
  Raspberry Pi Pico: Raspberry Pi Pico. Based around the RP2040 microcontroller the Pico is a low cost microcontroller device bringing Raspberry Pi quality, cost, and easy of use to the microcontroller space.
  KY-033 Line Tracking Sensor Module: KY-033 line tracking sensor module. An infrared sensor used to detect opaque surfaces.
