# Fritzing sketch KY-034_7_Color_Flash (saved by Fritzing 0.9.3b)

parts:
  Pico1 = Raspberry Pi Pico
  Mod1 = KY-034 Automatic Flashing Color LED [package="Breakout board"]

nets:
  N1: Pico1.GND, Mod1.-
  N2: Pico1.GP0, Mod1.S

custom parts:
  Raspberry Pi Pico: Raspberry Pi Pico. Based around the RP2040 microcontroller the Pico is a low cost microcontroller device bringing Raspberry Pi quality, cost, and easy of use to the microcontroller space.
  KY-034 Automatic Flashing Color LED: KY-034 Automatic Flashiing Color LED. A 7 color LED that flashes through a sequence of colors, creating a multicolored pattern of flashing light.
